// Logisim project 6.circ as structural Verilog: 1 circuit, main circuit main
module main (
  input  \输入_1 ,
  input  \输入_2 ,
  output \输出_1 ,
  output \输出_2 ,
  output \输出_3 ,
  output \引脚_A ,
  output \引脚_B 
);

  wire a_q, buffer_1_out, buffer_2_out, CLK_out, decoder_1_out1, decoder_1_out2, decoder_1_out3,
       decoder_2_out1, decoder_2_out2, decoder_2_out3, decoder_3_out1, decoder_3_out2, decoder_3_out3,
       multiplexer_2_out, ram_1_data;
  wire [0:0] multiplexer_1_out;

  Clock CLK (.out(CLK_out));
  Multiplexer multiplexer_1 (.in0(buffer_2_out), .in1(1'b1), .out(multiplexer_1_out[0]), .sel(1'b0));  // open: en
  RAM #(.addrWidth(2), .dataWidth(1)) ram_1 (
    .addr({1'b1, multiplexer_1_out[0]}), .data(ram_1_data));  // open: sel, clk, ld, clr
  D_Flip_Flop a (.clk(CLK_out), .D(ram_1_data), .Q(a_q));  // open: Qn, preset, en, reset
  Multiplexer multiplexer_2 (.in0(a_q), .in1(ram_1_data), .out(multiplexer_2_out), .sel(1'b0));  // open: en
  Decoder #(.select(2)) decoder_1 (
    .out1(decoder_1_out1), .out2(decoder_1_out2), .out3(decoder_1_out3), .sel(2'b11));  // open: out0, en
  assign \输出_1  = decoder_1_out1 ? \输入_1  : 1'bz;  // Controlled_Buffer controlled_buffer_1
  assign \输出_1  = decoder_1_out2 ? \输入_2  : 1'bz;  // Controlled_Buffer controlled_buffer_2
  assign \输出_1  = decoder_1_out3 ? multiplexer_2_out : 1'bz;  // Controlled_Buffer controlled_buffer_3
  assign \输出_2  = decoder_2_out1 ? \输入_1  : 1'bz;  // Controlled_Buffer controlled_buffer_4
  assign \输出_2  = decoder_2_out2 ? \输入_2  : 1'bz;  // Controlled_Buffer controlled_buffer_5
  assign \输出_2  = decoder_2_out3 ? multiplexer_2_out : 1'bz;  // Controlled_Buffer controlled_buffer_6
  Decoder #(.select(2)) decoder_2 (
    .out1(decoder_2_out1), .out2(decoder_2_out2), .out3(decoder_2_out3), .sel(2'b10));  // open: out0, en
  Decoder #(.select(2)) decoder_3 (
    .out1(decoder_3_out1), .out2(decoder_3_out2), .out3(decoder_3_out3), .sel(2'b01));  // open: out0, en
  assign \输出_3  = decoder_3_out1 ? \输入_1  : 1'bz;  // Controlled_Buffer controlled_buffer_7
  assign \输出_3  = decoder_3_out2 ? \输入_2  : 1'bz;  // Controlled_Buffer controlled_buffer_8
  assign \输出_3  = decoder_3_out3 ? multiplexer_2_out : 1'bz;  // Controlled_Buffer controlled_buffer_9
  buf buffer_1 (buffer_1_out, \引脚_A );
  assign \引脚_A  = 1'b1 ? \输出_2  : 1'bz;  // Controlled_Buffer controlled_buffer_10
  buf buffer_2 (buffer_2_out, \引脚_B );
  assign \引脚_B  = 1'b1 ? \输出_1  : 1'bz;  // Controlled_Buffer controlled_buffer_11

  // Notes on the sheet:
  //   a
  //   b
endmodule
